# Fritzing sketch Untitled Sketch 2 (saved by Fritzing 0.9.3b)
breadboards: 1

parts:
  부품1 = Arduino Nano (Rev3.0)
  부품2 = Bluetooth HC-05 Macho
  J1 = Basic Force Sensing Resistor (FSR) [package=THT]
  U1 = Vibration Motor- ROB-08449 [package=vibe-motor-10mm]
  R1 = Resistor [tolerance=±5% resistance=5k package=THT]

nets:
  GND: 부품1.GND, 부품2.GND, U1.+, R1.Pin_1
  N1: 부품1.D2, 부품2.TXD
  N2: 부품1.D3, 부품2.RXD
  N3: 부품1.D7, U1.-
  5V: 부품1.5V, 부품2.VCC, J1.pin_0
  N4: 부품1.A0, J1.pin_1, R1.Pin_0

notes:
  Vibration motor
